# Fritzing sketch MFSD_Buzzer-Test_v1 (saved by Fritzing 0.9.4)
breadboards: 1

parts:
  Arduino328 = Arduino Uno (Rev3)
  MFS1 = Multi Function Shield  # not connected

nets:
  GND: Arduino328.GND
  +5V: Arduino328.5V

notes:
  El botón 3 activa el zumbador

custom parts:
  Multi Function Shield: Das Multi Function Shield kann auf den Arduino Uno aufgesteckt werden und bietet ein paar wichtige Bauteile.

// code stored in the sketch: Blinking-LED_v1.ino
int led1=13;
int led2=12;
int led3=11;
int led4=10;

void setup() {
  pinMode(led1,OUTPUT);
  pinMode(led2,OUTPUT);
  pinMode(led3,OUTPUT);
  pinMode(led4,OUTPUT);
}

void loop() {
  digitalWrite(led1,HIGH);
  delay(1000);
  digitalWrite(led1,LOW);
  digitalWrite(led2,HIGH);
  delay(1000);
  digitalWrite(led2,LOW);
  digitalWrite(led3,HIGH);
  delay(1000);
  digitalWrite(led3,LOW);
  digitalWrite(led4,HIGH);
  delay(1000);
  digitalWrite(led4,LOW);
}

// code stored in the sketch: Buzzer-Test_v1.ino
//ARMUINO: El botón 3 activa el zumbador
#define BUZZER 3 // El zumbador está en el pin D3
#define BUTTON A3 // El botón está en el pin A3

void setup() {
  pinMode(BUTTON, INPUT);
  pinMode(BUZZER, OUTPUT);
  digitalWrite(BUZZER,HIGH); //Apaga el zumbador
}

void loop() {
  if(!digitalRead(BUTTON)){
    digitalWrite(BUZZER,LOW);//Enciende el zumbador
  }
  else{
    digitalWrite(BUZZER,HIGH); //Apaga el zumbador
  }
}

// code stored in the sketch: Codigo_alarma_gas_metano_MFS.ino
/* Alarma de Gas Metano

Hecho por:  http://elprofegarcia.com/
Conecta el Arduino con el Sensor de Gas MQ4 y cuando el nivel de concentracion de gas metano 
Supera un limite se activa una alarma sonora, el nivel de gas metado se puede visualizar por
el Monitor Serial.
Conexiones:
ARDUINO      MQ4      Zumbador

5V           Vcc
GND          GND
A5           A0

Pin 3                  +
GND                    GND

Componentes Comprados en: http://dinastiatecnologica.com/
*/

int valor_limite= 200;                  // Fiaja el valor limite en el que se activa la alarma    
                                        // Fije el valor despues de visualizar el nivel con el Monitor Serial
void setup() { 
  Serial.begin(9600);                   // Activa el puerto Serial a 9600 Baudios
  pinMode(3,OUTPUT);                   // Configura el Pin 3 como salida para el Zumbador
}

void loop() { 
  Serial.println(analogRead(A5));       // Envia al Serial el valor leido del Sensor MQ4 
 
  if(analogRead(A5) > valor_limite){    // Si la medida de gas metano es mayor de valor limite
       digitalWrite(3, LOW);          // Enciende el Zumbador conectado al Pin 13
   }
   else{                                // Si es menor del valor limite apaga el Zumbador
      digitalWrite(3,HIGH); 
   }
  delay (300);                          // Espera 300ms para realizar la proxima medida
}

// code stored in the sketch: Test-Switches_v1.ino
//ARMUINO: Boton 1- todos apagados;Boton 2 - todos encendidos
int led1=13; int led2=12; int led3=11; int led4=10;

#define BTN1 A1
#define BTN2 A2
#define BTN3 A3

void setup() {
  Serial.begin(9600);
  pinMode(led1,OUTPUT);
  pinMode(led2,OUTPUT);
  pinMode(led3,OUTPUT);
  pinMode(led4,OUTPUT);
}

void loop() {
  if(!digitalRead(BTN1)){
    Serial.println("Boton 1 oprimido: Todos Apagados");
    digitalWrite(led1,HIGH);
    digitalWrite(led2,HIGH);
    digitalWrite(led3,HIGH);
    digitalWrite(led4,HIGH);    
  }
  if(!digitalRead(BTN2)){
    Serial.println("Boton 2 oprimido: Todos Encendidos");
    digitalWrite(led1,LOW);
    digitalWrite(led2,LOW);
    digitalWrite(led3,LOW);
    digitalWrite(led4,LOW);    
  }
}
