# Fritzing sketch Led Matrix simulation with max7219 in proteus (saved by Fritzing 0.9.4)
breadboards: 1

parts:
  Arduino_Genuino_UNO = Arduino Uno (Rev3)
  8x8_LED_Modul_mit_MAX1 = 8x8 LED Modul mit MAX7219 [package=THT]

nets:
  Chip Select: Arduino_Genuino_UNO.D10_PWM/SS, 8x8_LED_Modul_mit_MAX1.CS_Eingang
  Clock: Arduino_Genuino_UNO.D11_PWM/MOSI, 8x8_LED_Modul_mit_MAX1.CLK_Eingang
  Data In: Arduino_Genuino_UNO.D12/MISO, 8x8_LED_Modul_mit_MAX1.DIN_Eingang
  GND: Arduino_Genuino_UNO.GND, 8x8_LED_Modul_mit_MAX1.GND_Eingang
  +5V: Arduino_Genuino_UNO.5V, 8x8_LED_Modul_mit_MAX1.VCC_Eingang

// code stored in the sketch: scroll.ino
#include <MatrizLed.h>

/*
 * Texto que aparece por la derecha y sale por la izquierda
 */

MatrizLed pantalla;

void setup() {
  pantalla.begin(12, 11, 10, 1); // dataPin, clkPin, csPin, numero de matrices de 8x8
}

void loop() { 
  pantalla.borrar();
  pantalla.escribirFraseScroll("Hola Mundo", 200); // Texto, milisegundos entre frames
}
