# Fritzing sketch Traffic-light-demonstration (saved by Fritzing 0.9.4)
breadboards: 1

parts:
  Componente1 = Arduino Uno (Rev3)
  LED2 = LED - 5mm [color="Red (633nm)" package="5 mm [THT]"]
  R1 = Resistor [tolerance=±5% resistance=220 package="0402 [SMD]"]
  LED3 = LED - 5mm [color="Yellow (585nm)" package="5 mm [THT]"]
  R2 = Resistor [tolerance=±5% resistance=220 package="0402 [SMD]"]
  LED4 = LED - 5mm [color="Green (555nm)" package="5 mm [THT]"]
  R3 = Resistor [tolerance=±5% resistance=220 package="0402 [SMD]"]
  R4 = Resistor [tolerance=±5% resistance=220 package=THT]
  LED5 = LED - 5mm [color="Red (633nm)" package="5 mm [THT]"]
  R6 = Resistor [tolerance=±5% resistance=220 package=THT]
  LED7 = LED - 5mm [color="Yellow (585nm)" package="5 mm [THT]"]
  LED8 = LED - 5mm [color="Green (555nm)" package="5 mm [THT]"]
  R7 = Resistor [tolerance=±5% resistance=220 package=THT]
  LED9 = LED - 5mm [color="Red (633nm)" package="5 mm [THT]"]
  R8 = Resistor [tolerance=±5% resistance=220 package=THT]
  LED10 = LED - 5mm [color="Yellow (585nm)" package="5 mm [THT]"]
  R9 = Resistor [tolerance=±5% resistance=220 package=THT]
  LED11 = LED - 5mm [color="Green (555nm)" package="5 mm [THT]"]
  R10 = Resistor [tolerance=±5% resistance=220 package=THT]
  LED14 = LED - 5mm [color="Red (633nm)" package="5 mm [THT]"]
  R11 = Resistor [tolerance=±5% resistance=220 package=THT]
  R12 = Resistor [tolerance=±5% resistance=220 package=THT]
  LED13 = LED - 5mm [color="Yellow (585nm)" package="5 mm [THT]"]
  R13 = Resistor [tolerance=±5% resistance=220 package=THT]
  LED12 = LED - 5mm [color="Green (555nm)" package="5 mm [THT]"]

nets:
  N1: Componente1.D8, LED13.anode
  N2: Componente1.D9_PWM, LED12.anode
  N3: Componente1.D10_PWM/SS, R8.Pin_1
  N4: Componente1.D11_PWM/MOSI, R9.Pin_1
  N5: Componente1.D12/MISO, R10.Pin_1
  N6: Componente1.D1/TX, LED2.anode
  N7: Componente1.D2, LED3.anode
  N8: Componente1.D3_PWM, LED4.anode
  N9: Componente1.D4, R4.Pin_0
  N10: Componente1.D5_PWM, R6.Pin_0
  N11: Componente1.D6_PWM, R7.Pin_0
  N12: Componente1.D7, LED14.anode
  GND: Componente1.GND, R1.Pin_0, R2.Pin_0, R3.Pin_0, LED5.cathode, LED7.cathode, LED8.cathode, LED9.cathode, LED10.cathode, LED11.cathode, R11.Pin_0, R12.Pin_0, R13.Pin_0
  N13: LED2.cathode, R1.Pin_1
  N14: LED3.cathode, R2.Pin_1
  N15: LED4.cathode, R3.Pin_1
  N16: R4.Pin_1, LED5.anode
  N17: R6.Pin_1, LED7.anode
  N18: LED8.anode, R7.Pin_1
  N19: LED9.anode, R8.Pin_0
  N20: LED10.anode, R9.Pin_0
  N21: LED11.anode, R10.Pin_0
  N22: LED14.cathode, R11.Pin_1
  N23: R12.Pin_1, LED13.cathode
  N24: R13.Pin_1, LED12.cathode
