# Fritzing sketch KY-012 (saved by Fritzing 0.9.4)
breadboards: 1

parts:
  Arduino328 = Arduino Uno (Rev3)
  Active_Buzzer_Module = KY-012 Active Buzzer Module [package="Breakout board"]
  3906 = PNP-Transistor [part_number=Q1 package="SOT-23 [SMD]"]
  R1 = Resistor [tolerance=±10% resistance=10k package=THT]

nets:
  N1: Arduino328.D9_PWM, R1.Pin_0
  GND: Arduino328.GND, Active_Buzzer_Module.-
  +5V: Arduino328.5V, 3906.2
  N2: Active_Buzzer_Module.S, 3906.1
  N3: 3906.0, R1.Pin_1

custom parts:
  KY-012 Active Buzzer Module: Active Piezoelectric Buzzer Module Keyes KY-012, it produces single-tone sound when signal is high.

// code stored in the sketch: Codigo_alarma_gas_metano_MFS.ino
/* Alarma de Gas Metano

Hecho por:  http://elprofegarcia.com/
Conecta el Arduino con el Sensor de Gas MQ4 y cuando el nivel de concentracion de gas metano 
Supera un limite se activa una alarma sonora, el nivel de gas metado se puede visualizar por
el Monitor Serial.
Conexiones:
ARDUINO      MQ4      Zumbador

5V           Vcc
GND          GND
A5           A0

Pin 3                  +
GND                    GND

Componentes Comprados en: http://dinastiatecnologica.com/
*/

int valor_limite= 200;                  // Fiaja el valor limite en el que se activa la alarma    
                                        // Fije el valor despues de visualizar el nivel con el Monitor Serial
void setup() { 
  Serial.begin(9600);                   // Activa el puerto Serial a 9600 Baudios
  pinMode(3,OUTPUT);                   // Configura el Pin 3 como salida para el Zumbador
}

void loop() { 
  Serial.println(analogRead(A5));       // Envia al Serial el valor leido del Sensor MQ4 
 
  if(analogRead(A5) > valor_limite){    // Si la medida de gas metano es mayor de valor limite
       digitalWrite(3, LOW);          // Enciende el Zumbador conectado al Pin 13
   }
   else{                                // Si es menor del valor limite apaga el Zumbador
      digitalWrite(3,HIGH); 
   }
  delay (300);                          // Espera 300ms para realizar la proxima medida
}

// code stored in the sketch: KY-012_Serial-Monitor.ino
int BUZZER=9;
int i;

void setup() {
  pinMode(BUZZER,OUTPUT);
  Serial.begin(9600);
}

void loop() {
  for(i=255;i>=0;i--){
    Serial.print(i);
    Serial.print(" : ");
    Serial.println(i*100/255);
    Serial.print("%");
    analogWrite(BUZZER,i); //0=ON 255=OFF
    delay(50);
    analogWrite(BUZZER,255);
  }
}

// code stored in the sketch: MFS-Buzzer_Experiment.ino
//*******************************************************************************
//----------------Este ejemplo es solo para fines de aprendizaje y no se puede utilizar para otros fines sin el permiso del autor.-----------
//------------------------Derechos de autor, falsificación serán investigados!-----------------------------------
//----------------1.Entorno de desarrollo:Arduino IDE-----------------------------------------
//----------------2.Prueba usando el modelo de la placa de desarrollo：Arduino Leonardo or Arduino UNO R3-------
//----------------3.El microcontrolador usa un oscilador de cristal：16M------------------------------------------
//----------------4.Sitio web de Taobao：http://xmdzpj.taobao.com---------------------------
//----------------5.Autor: Dios realmente la inflamación roja---------------------------------------------
//*******************************************************************************/

int buzzer=3;     //Establecer el pin IO digital que controla el zumbador
void setup() 
{ 
pinMode(buzzer,OUTPUT);//Establezca el modo digital IO pin, OUTPUT es la salida
} 
void loop() 
{ 
unsigned char i,j;//Definiendo variables
while(1) 
{ 
for(i=0;i<80;i++)//Salida una frecuencia de sonido
{ 
digitalWrite(buzzer,HIGH);//Sonido
delay(10);//Demora 1ms
digitalWrite(buzzer,LOW);//Sin sonido
delay(10);//Retraso ms
} 
for(i=0;i<100;i++)//Salida otra frecuencia de sonido
{ 
digitalWrite(buzzer,HIGH);//Sonido
delay(20);//延时2ms 
digitalWrite(buzzer,LOW);//Sin sonido
delay(20);//Demora 2ms
} 
} 
}
